# Fritzing sketch GyroClock (saved by Fritzing 0.9.2b)
breadboards: 1

parts:
  RTC = Real Time Clock Module - DS1307 RTC Breakout Board
  Arduino_Uno = Arduino Uno (Rev3) - ICSP
  Segment_screen = Grove 4 Digit Display
  GY1 = MPU-6050 Board GY-521 [form="♀ (female)" package=THT]

nets:
  5V: RTC.5V, Arduino_Uno.5V, Segment_screen.VCC, GY1.pin1, GY1.pin7
  GND: RTC.GND, Arduino_Uno.GND, Segment_screen.GND, GY1.pin2
  N1: RTC.SCL, Arduino_Uno.A5/SCL, GY1.pin3
  N2: RTC.SDA, Arduino_Uno.A4/SDA, GY1.pin4
  N3: Arduino_Uno.D3_PWM, Segment_screen.DIO
  N4: Arduino_Uno.D4, Segment_screen.CLK

custom parts:
  MPU-6050 Board GY-521: Acelerometro y Giroscopio MPU-6050 Board GY-521
